# Fritzing sketch AR02_2LED (saved by Fritzing 0.9.3b)
breadboards: 1

parts:
  R1 = Resistor [tolerance=±5% resistance=330 package=THT]
  R2 = Resistor [tolerance=±5% resistance=330 package=THT]
  LED1 = smd LED [color="Red (633nm)" package="1206 [SMD]"]
  부품1 = Arduino Uno (Rev3)
  LED2 = LED - 5mm [color="Green (570nm)" package="5 mm [THT]"]

nets:
  N1: R1.Pin_0, R2.Pin_1, 부품1.GND, LED2.cathode
  N2: R1.Pin_1, LED1.cathode
  N3: LED1.anode, 부품1.D5_PWM
  N4: 부품1.D3_PWM, LED2.anode
