# Fritzing sketch AR02_4LED (saved by Fritzing 0.9.3b)
breadboards: 1

parts:
  R1 = Resistor [tolerance=±5% resistance=330 package=THT]
  R2 = Resistor [tolerance=±5% resistance=330 package=THT]
  LED1 = smd LED [color="Red (633nm)" package="1206 [SMD]"]
  부품1 = Arduino Uno (Rev3)
  LED2 = LED - 5mm [color="Green (570nm)" package="5 mm [THT]"]
  R3 = Resistor [tolerance=±5% resistance=330 package=THT]
  R4 = Resistor [tolerance=±5% resistance=330 package=THT]
  LED3 = smd LED [color="Yellow (595nm)" package="1206 [SMD]"]
  LED4 = smd LED [color="Blue (525nm)" package="1206 [SMD]"]

nets:
  N1: R1.Pin_0, R2.Pin_0, 부품1.GND, R3.Pin_0, R4.Pin_0
  N2: R1.Pin_1, LED1.cathode
  N3: R2.Pin_1, LED4.cathode
  N4: LED1.anode, 부품1.D6_PWM
  N5: 부품1.D9_PWM, LED3.anode
  N6: 부품1.D3_PWM, LED4.anode
  N7: 부품1.D5_PWM, LED2.anode
  N8: LED2.cathode, R4.Pin_1
  N9: R3.Pin_1, LED3.cathode
