# Fritzing sketch AR02_RGB (saved by Fritzing 0.9.3b)
breadboards: 1

parts:
  부품1 = Arduino Uno (Rev3)
  LED2 = Super Flux RGB LED (com. cathode)

nets:
  N1: 부품1.D3_PWM, LED2.blue_anode
  N2: 부품1.D5_PWM, LED2.red_anode
  N3: 부품1.D6_PWM, LED2.green_anode
  N4: 부품1.GND, LED2.common_cathode
