# Fritzing sketch clock (saved by Fritzing 0.9.3b)
breadboards: 1

parts:
  부품1 = Arduino Uno (Rev3)
  J1 = Piezo Speaker
  LCD1 = LCD screen
  LED1 = smd LED [color="White (4500K)" package="0603 [SMD]"]
  R1 = Resistor [tolerance=±5% resistance=330 package=THT]
  S1 = Pushbutton [package="[THT]"]

nets:
  N1: 부품1.A4/SDA, LCD1.V0
  N2: 부품1.A5/SCL, LCD1.RS
  N3: 부품1.D9_PWM, J1.pin2
  N4: 부품1.D13/SCK, LED1.anode
  N5: 부품1.D2, S1.Pin_1, S1.Pin_2
  5V: 부품1.5V, LCD1.VDD
  GND: 부품1.GND, J1.pin1, LCD1.VSS, R1.Pin_1, S1.Pin_3, S1.Pin_4
  N6: LED1.cathode, R1.Pin_0
